// Logisim project cpu.circ as structural Verilog: 33 circuits, main circuit main
// CPU
module main (
  input  [31:0] RS_READ_VALUE,
  input  [31:0] RI_READ_VALUE,
  input  [31:0] RD_READ_VALUE,
  input  [31:0] JC_READ_VALUE,
  input  [31:0] INSTRUCTION,
  input  CLOCK,
  output [4:0] RS,
  output [4:0] RI,
  output [4:0] RD,
  output [31:0] RD_WRITE_VALUE,
  output RD_WRITE_ENABLE,
  output [23:0] FETCH_ADDRESS
);

  wire and_1_out, J, JAL, JUMP, MemToReg, MemWrite, ra, RegWrite, u_control_j_1_out_2, u_control_r_1_out_2,
       W_MODE;
  wire [2:0] JC;
  wire [4:0] RD_t, RI_J, RI_R;
  wire [16:0] IMM;
  wire [23:0] ADDRESS, IMM_R, PC, PC_1;
  wire [31:0] bit_extender_1_out, bit_extender_2_out, MemData, multiplexer_2_out, multiplexer_6_out, RD_FINAL;

  or or_1 (RD_WRITE_ENABLE, RegWrite, ra);
  Adder #(.width(24)) adder_1 (.a(FETCH_ADDRESS), .b(24'h1), .out(PC_1));  // open: cin, cout
  Register #(.width(24)) register_1 (.D(PC), .Q(FETCH_ADDRESS), .clk(CLOCK));  // open: en, clr
  Multiplexer #(.width(24), .enable("false")) multiplexer_1 (.in0(PC_1), .in1(ADDRESS), .out(PC), .sel(and_1_out));
  and and_1 (and_1_out, J, JUMP);
  Multiplexer #(.width(32)) multiplexer_2 (
    .in0(RD_FINAL), .in1(MemData), .out(multiplexer_2_out), .sel(MemToReg));  // open: en
  assign bit_extender_1_out = {{8{PC_1[23]}}, PC_1};  // Bit_Extender bit_extender_1
  Multiplexer #(.width(32)) multiplexer_3 (
    .in0(multiplexer_2_out), .in1(bit_extender_1_out), .out(RD_WRITE_VALUE), .sel(ra));  // open: en
  and and_2 (ra, JAL, JUMP);
  assign bit_extender_2_out = {{15{IMM[16]}}, IMM};  // Bit_Extender bit_extender_2
  u_CONTROL_R u_control_r_1 (
    .in_1(INSTRUCTION[27:0]), .out_2(u_control_r_1_out_2), .RD(RD_t), .RS(RS), .RI(RI_R), .out_6(IMM));
  u_CONTROL_J u_control_j_1 (.in_1(INSTRUCTION[27:0]), .out_2(u_control_j_1_out_2), .JC(JC), .RI(RI_J), .out_5(IMM_R));
  Multiplexer #(.width(24)) multiplexer_4 (
    .in0(RI_READ_VALUE[23:0]), .in1(IMM_R), .out(ADDRESS), .sel(u_control_j_1_out_2));  // open: en
  Multiplexer #(.width(5)) multiplexer_5 (.in0(RD_t), .in1(5'b00110), .out(RD), .sel(ra));  // open: en
  Multiplexer #(.width(32), .enable("false")) multiplexer_6 (
    .in0(RI_READ_VALUE), .in1(bit_extender_2_out), .out(multiplexer_6_out), .sel(u_control_r_1_out_2));
  and and_3 (JAL, JC[0], JC[1], JC[2]);
  u_ALU u_alu_1 (
    .ALU_X(RS_READ_VALUE), .ALU_Y(multiplexer_6_out), .ALU_RESULT(RD_FINAL), .ALU_CONTROL(INSTRUCTION[31:28]));
  u_CONTROL u_control_1 (
    .in_1(INSTRUCTION[31:28]), .MemWrite(MemWrite), .RegWrite(RegWrite), .MemtoReg(MemToReg), .JUMP(JUMP),
    .WordMode(W_MODE));
  u_JUMPS u_jumps_1 (.in_1(JC_READ_VALUE), .in_2(JC), .out_3(J));
  u_MEM u_mem_1 (
    .ADDRESS(RD_FINAL[24:0]), .WORD_MODE(W_MODE), .MEM_WRITE(MemWrite), .DATA_IN(RD_READ_VALUE),
    .CLOCK(CLOCK), .DATA_OUT(MemData));
  Multiplexer #(.width(5)) multiplexer_7 (.in0(RI_R), .in1(RI_J), .out(RI), .sel(JUMP));  // open: en

  // Other names for the same wires on the sheet: CLK = CLOCK; ALUctrl[3:0] = INSTRUCTION[31:28];
  //   JC_read[31:0] = JC_READ_VALUE; RD_F[4:0] = RD; RD_VALUE[31:0] = RD_READ_VALUE; reg[23:0] = FETCH_ADDRESS;
  //   RI_READ[31:0] = RI_READ_VALUE; w_value[31:0] = RD_WRITE_VALUE
endmodule

module u_ALU (
  input  [31:0] ALU_X,
  input  [31:0] ALU_Y,
  input  [3:0] ALU_CONTROL,
  output [31:0] ALU_RESULT
);

  wire [31:0] ADD, AND, DIV, MUL, OR, REV, SL, SR, STU, SUB, XOR;

  u_SL u_sl_1 (.in_1(ALU_X), .in_2(ALU_Y), .out_3(SL));
  u_ADD u_add_1 (.in_1(ALU_X), .in_2(ALU_Y), .out_3(ADD));
  u_SR u_sr_1 (.in_1(ALU_X), .in_2(ALU_Y), .out_3(SR));
  u_AND u_and_1 (.in_1(ALU_X), .in_2(ALU_Y), .out_3(AND));
  u_OR u_or_1 (.in_1(ALU_X), .in_2(ALU_Y), .out_3(OR));
  u_XOR u_xor_1 (.in_1(ALU_X), .in_2(ALU_Y), .out_3(XOR));
  u_SUB u_sub_1 (.in_1(ALU_X), .in_2(ALU_Y), .out_3(SUB));
  u_MUL u_mul_1 (.in_1(ALU_X), .in_2(ALU_Y), .out_3(MUL));
  u_DIV u_div_1 (.in_1(ALU_X), .in_2(ALU_Y), .out_3(DIV));
  u_REV u_rev_1 (.INPUT(ALU_X), .REVERSE_AMOUNT(ALU_Y[4:0]), .OUTPUT(REV));
  u_STU u_stu_1 (.in_1(ALU_X), .in_2(ALU_Y), .out_3(STU));
  Multiplexer #(.select(4), .width(32)) multiplexer_1 (
    .in0(SL), .in1(SR), .in2(AND), .in3(OR), .in4(REV), .in5(XOR), .in6(ADD), .in7(SUB), .in8(MUL),
    .in9(DIV), .in10(ADD), .in11(ADD), .in12(ADD), .in13(ADD), .in14(STU), .out(ALU_RESULT), .sel(ALU_CONTROL));  // open: in15, en
endmodule

// Data Memory
module u_MEM (
  input  [24:0] ADDRESS,
  input  WORD_MODE,
  input  MEM_WRITE,
  input  [31:0] DATA_IN,
  input  CLOCK,
  output [31:0] DATA_OUT
);

  wire and_1_out, and_2_out, and_3_out, and_4_out, and_5_out, and_6_out, not_1_out, not_2_out, not_3_out,
       or_1_out, or_2_out, undriven;
  wire [15:0] FINAL_E_D, FINAL_O_D, Low_E, Low_O, Upper_E, Upper_O;
  wire [23:0] EVEN, EVEN_1, FINAL_E, FINAL_O, ODD, ODD_1;
  wire [24:0] ADD_1;
  wire [31:0] bit_extender_1_out, bit_extender_2_out, multiplexer_4_out, OUT_1, OUT_WM;

  Adder #(.width(25)) adder_1 (.a(ADDRESS), .b(25'h1), .out(ADD_1));  // open: cin, cout
  Demultiplexer #(.width(24), .enable("false")) demultiplexer_1 (
    .out0(EVEN), .out1(ODD), .in(ADDRESS[24:1]), .sel(ADDRESS[0]));
  Demultiplexer #(.width(24), .enable("false")) demultiplexer_2 (
    .out0(EVEN_1), .out1(ODD_1), .in(ADD_1[24:1]), .sel(ADD_1[0]));
  and and_1 (and_1_out, MEM_WRITE, or_1_out);
  or or_1 (or_1_out, ADDRESS[0], WORD_MODE);
  Demultiplexer #(.width(16)) demultiplexer_3 (
    .out0(Low_E), .out1(Low_O), .in(DATA_IN[15:0]), .sel(ADDRESS[0]));  // open: en
  RAM #(.addrWidth(24), .dataWidth(16), .bus("separate")) ram_1 (
    .addr(FINAL_O), .din(FINAL_O_D), .data(OUT_1[15:0]), .str(and_1_out), .clk(CLOCK));  // open: sel, ld, clr
  Multiplexer #(.width(24)) multiplexer_1 (.in0(EVEN), .in1(EVEN_1), .out(FINAL_E), .sel(and_2_out));  // open: en
  Multiplexer #(.width(32)) multiplexer_2 (
    .in0({OUT_1[15:0], OUT_1[31:16]}), .in1(OUT_1), .out(OUT_WM), .sel(ADDRESS[0]));  // open: en
  and and_2 (and_2_out, ADDRESS[0], WORD_MODE);
  and and_3 (and_3_out, MEM_WRITE, or_2_out);
  or or_2 (or_2_out, not_1_out, WORD_MODE);
  not not_1 (not_1_out, ADDRESS[0]);
  Demultiplexer #(.width(16)) demultiplexer_4 (
    .out0(Upper_E), .out1(Upper_O), .in(DATA_IN[31:16]), .sel(ADD_1[0]));  // open: en
  assign bit_extender_1_out = {{16{OUT_1[31]}}, OUT_1[31:16]};  // Bit_Extender bit_extender_1
  assign bit_extender_2_out = {{16{OUT_1[15]}}, OUT_1[15:0]};  // Bit_Extender bit_extender_2
  Multiplexer #(.width(24)) multiplexer_3 (.in0(ODD), .in1(ODD_1), .out(FINAL_O), .sel(and_4_out));  // open: en
  not not_2 (not_2_out, ADDRESS[0]);
  Multiplexer #(.width(32)) multiplexer_4 (
    .in0(bit_extender_1_out), .in1(bit_extender_2_out), .out(multiplexer_4_out), .sel(ADDRESS[0]));  // open: en
  RAM #(.addrWidth(24), .dataWidth(16), .bus("separate")) ram_2 (
    .addr(FINAL_E), .din(FINAL_E_D), .data(OUT_1[31:16]), .str(and_3_out), .clk(CLOCK), .ld(undriven));  // open: sel, clr
  and and_4 (and_4_out, not_2_out, WORD_MODE);
  Multiplexer #(.width(32)) multiplexer_5 (
    .in0(multiplexer_4_out), .in1(OUT_WM), .out(DATA_OUT), .sel(WORD_MODE));  // open: en
  Multiplexer #(.width(16)) multiplexer_6 (.in0(Low_E), .in1(Upper_E), .out(FINAL_E_D), .sel(and_5_out));  // open: en
  and and_5 (and_5_out, ADDRESS[0], WORD_MODE);
  Multiplexer #(.width(16)) multiplexer_7 (.in0(Low_O), .in1(Upper_O), .out(FINAL_O_D), .sel(and_6_out));  // open: en
  not not_3 (not_3_out, ADDRESS[0]);
  and and_6 (and_6_out, not_3_out, WORD_MODE);

  // Other names for the same wires on the sheet: BIT_1 = ADD_1[0]; BIT = ADDRESS[0]; CLK = CLOCK;
  //   Lower[15:0] = DATA_IN[15:0]; Upper[15:0] = DATA_IN[31:16]; MW = MEM_WRITE;
  //   OUT_2[31:0] = {OUT_1[15:0], OUT_1[31:16]}; OUT_D_E[15:0] = OUT_1[31:16]; OUT_D_O[15:0] = OUT_1[15:0];
  //   WM = WORD_MODE
endmodule

module u_REV (
  input  [31:0] INPUT,
  input  [4:0] REVERSE_AMOUNT,
  output [31:0] OUTPUT
);

  u_REV_main u_rev_main_1 (.in_1(INPUT), .out_3(OUTPUT), .in_2(REVERSE_AMOUNT));
endmodule

module u_CONTROL (
  input  [3:0] in_1,
  output MemWrite,
  output RegWrite,
  output MemtoReg,
  output JUMP,
  output WordMode
);

  wire ADD, AND, DIV, LH, LW, MUL, not_1_out, not_2_out, not_3_out, not_4_out, OR, REV, SH, SL, SR, STU, SUB,
       SW, XOR;

  not not_1 (not_1_out, in_1[3]);
  not not_2 (not_2_out, in_1[2]);
  not not_3 (not_3_out, in_1[1]);
  not not_4 (not_4_out, in_1[0]);
  and and_1 (SL, not_4_out, not_3_out, not_2_out, not_1_out);
  and and_2 (LH, not_4_out, in_1[1], not_2_out, in_1[3]);
  and and_3 (SH, in_1[0], in_1[1], not_2_out, in_1[3]);
  and and_4 (SW, in_1[0], not_3_out, in_1[2], in_1[3]);
  and and_5 (LW, not_4_out, not_3_out, in_1[2], in_1[3]);
  and and_6 (JUMP, in_1[0], in_1[1], in_1[2], in_1[3]);
  and and_7 (SR, in_1[0], not_3_out, not_2_out, not_1_out);
  and and_8 (AND, not_4_out, in_1[1], not_2_out, not_1_out);
  and and_9 (OR, in_1[0], in_1[1], not_2_out, not_1_out);
  and and_10 (REV, not_4_out, not_3_out, in_1[2], not_1_out);
  and and_11 (XOR, in_1[0], not_3_out, in_1[2], not_1_out);
  and and_12 (ADD, not_4_out, in_1[1], in_1[2], not_1_out);
  and and_13 (SUB, in_1[0], in_1[1], in_1[2], not_1_out);
  and and_14 (MUL, not_4_out, not_3_out, not_2_out, in_1[3]);
  and and_15 (DIV, in_1[0], not_3_out, not_2_out, in_1[3]);
  and and_16 (STU, not_4_out, in_1[1], in_1[2], in_1[3]);
  or or_1 (MemWrite, SH, SW);
  or or_2 (MemtoReg, LH, LW);
  or or_3 (WordMode, LW, SW);
  or or_4 (RegWrite, SR, AND, ADD, OR, XOR, SL, STU, REV, LW, LH, SUB, DIV, MUL);
endmodule

module u_ADD (
  input  [31:0] in_1,
  input  [31:0] in_2,
  output [31:0] out_3
);

  Adder #(.width(32)) adder_1 (.a(in_1), .b(in_2), .out(out_3));  // open: cin, cout
endmodule

module u_SL (
  input  [31:0] in_1,
  input  [31:0] in_2,
  output [31:0] out_3
);

  u_SL_MAIN u_sl_main_1 (.in_1(in_1), .in_2(in_2[4:0]), .out_3(out_3));
endmodule

module u_SL_MAIN (
  input  [31:0] in_1,
  input  [4:0] in_2,
  output [31:0] out_3
);

  wire [31:0] u_sl_1_1_out_3, u_sl_2_1_out_3, u_sl_4_1_out_3, u_sl_8_1_out_3;

  u_SL_1 u_sl_1_1 (.in_1(in_1), .in_2(in_2[0]), .out_3(u_sl_1_1_out_3));
  u_SL_2 u_sl_2_1 (.in_1(u_sl_1_1_out_3), .in_2(in_2[1]), .out_3(u_sl_2_1_out_3));
  u_SL_4 u_sl_4_1 (.in_1(u_sl_2_1_out_3), .in_2(in_2[2]), .out_3(u_sl_4_1_out_3));
  u_SL_8 u_sl_8_1 (.in_1(u_sl_4_1_out_3), .in_2(in_2[3]), .out_3(u_sl_8_1_out_3));
  u_SL_16 u_sl_16_1 (.in_1(u_sl_8_1_out_3), .in_2(in_2[4]), .out_3(out_3));
endmodule

module u_SL_1 (
  input  [31:0] in_1,
  input  in_2,
  output [31:0] out_3
);

  Multiplexer #(.width(32), .enable("false")) multiplexer_1 (
    .in0(in_1), .in1({in_1[30:0], in_1[0]}), .out(out_3), .sel(in_2));

  // Other names for the same wires on the sheet: NEW[31:0] = {in_1[30:0], in_1[0]}; NUM[31:0] = in_1
endmodule

module u_SL_2 (
  input  [31:0] in_1,
  input  in_2,
  output [31:0] out_3
);

  Multiplexer #(.width(32), .enable("false")) multiplexer_1 (
    .in0(in_1), .in1({in_1[29:0], {2{in_1[0]}}}), .out(out_3), .sel(in_2));

  // Other names for the same wires on the sheet: NEW[31:0] = {in_1[29:0], {2{in_1[0]}}}; NUM[31:0] = in_1
endmodule

module u_SL_4 (
  input  [31:0] in_1,
  input  in_2,
  output [31:0] out_3
);

  Multiplexer #(.width(32), .enable("false")) multiplexer_1 (
    .in0(in_1), .in1({in_1[27:0], {4{in_1[0]}}}), .out(out_3), .sel(in_2));

  // Other names for the same wires on the sheet: NEW[31:0] = {in_1[27:0], {4{in_1[0]}}}; NUM[31:0] = in_1
endmodule

module u_SL_8 (
  input  [31:0] in_1,
  input  in_2,
  output [31:0] out_3
);

  Multiplexer #(.width(32), .enable("false")) multiplexer_1 (
    .in0(in_1), .in1({in_1[23:0], {8{in_1[0]}}}), .out(out_3), .sel(in_2));

  // Other names for the same wires on the sheet: NEW[31:0] = {in_1[23:0], {8{in_1[0]}}}; NUM[31:0] = in_1
endmodule

module u_SL_16 (
  input  [31:0] in_1,
  input  in_2,
  output [31:0] out_3
);

  Multiplexer #(.width(32), .enable("false")) multiplexer_1 (
    .in0(in_1), .in1({in_1[15:0], {16{in_1[0]}}}), .out(out_3), .sel(in_2));

  // Other names for the same wires on the sheet: NEW[31:0] = {in_1[15:0], {16{in_1[0]}}}; NUM[31:0] = in_1
endmodule

module u_AND (
  input  [31:0] in_1,
  input  [31:0] in_2,
  output [31:0] out_3
);

  assign out_3 = in_1 & in_2;  // AND_Gate and_1, 32 bits wide
endmodule

module u_OR (
  input  [31:0] in_1,
  input  [31:0] in_2,
  output [31:0] out_3
);

  assign out_3 = in_1 | in_2;  // OR_Gate or_1, 32 bits wide
endmodule

module u_XOR (
  input  [31:0] in_1,
  input  [31:0] in_2,
  output [31:0] out_3
);

  assign out_3 = in_1 ^ in_2;  // XOR_Gate xor_1, 32 bits wide
endmodule

module u_SUB (
  input  [31:0] in_1,
  input  [31:0] in_2,
  output [31:0] out_3
);

  Subtractor #(.width(32)) subtractor_1 (.a(in_1), .b(in_2), .out(out_3));  // open: bin, bout
endmodule

module u_MUL (
  input  [31:0] in_1,
  input  [31:0] in_2,
  output [31:0] out_3
);

  Multiplier #(.width(32)) multiplier_1 (.a(in_1), .b(in_2), .out(out_3));  // open: cin, cout
endmodule

module u_DIV (
  input  [31:0] in_1,
  input  [31:0] in_2,
  output [31:0] out_3
);

  wire comparator_1_eq, comparator_2_eq, comparator_3_eq, last;
  wire [30:0] multiplexer_4_out;
  wire [31:0] adder_1_out, adder_2_out, divider_1_out, multiplexer_3_out, multiplexer_5_out,
       multiplexer_7_out, not_1_out, not_2_out, not_3_out, NUM_1_r, NUM_2_r, subtractor_1_out;

  assign not_1_out = ~in_1;  // NOT_Gate not_1, 32 bits wide
  assign not_2_out = ~in_2;  // NOT_Gate not_2, 32 bits wide
  xor xor_1 (last, in_1[31], in_2[31]);
  Multiplexer #(.width(32), .enable("false")) multiplexer_1 (
    .in0(in_1), .in1(adder_1_out), .out(NUM_1_r), .sel(in_1[31]));
  Adder #(.width(32)) adder_1 (.a(not_1_out), .b(32'h1), .out(adder_1_out));  // open: cin, cout
  Multiplexer #(.width(32), .enable("false")) multiplexer_2 (
    .in0(in_2), .in1(adder_2_out), .out(NUM_2_r), .sel(in_2[31]));
  Adder #(.width(32)) adder_2 (.a(not_2_out), .b(32'h1), .out(adder_2_out));  // open: cin, cout
  // Probe on in_1
  // Probe on in_2
  // Probe on NUM_1_r
  // Probe on NUM_2_r
  Divider #(.width(32)) divider_1 (.a(NUM_1_r), .b(NUM_2_r), .out(divider_1_out));  // open: upper, rem
  assign not_3_out = ~subtractor_1_out;  // NOT_Gate not_3, 32 bits wide
  Subtractor #(.width(32)) subtractor_1 (.a(divider_1_out), .b(32'h1), .out(subtractor_1_out));  // open: bin, bout
  Comparator #(.width(32)) comparator_1 (.a(in_2), .b({32{1'b0}}), .eq(comparator_1_eq));  // open: gt, lt
  Multiplexer #(.width(32), .enable("false")) multiplexer_3 (
    .in0(divider_1_out), .in1(not_3_out), .out(multiplexer_3_out), .sel(last));
  Comparator #(.width(32)) comparator_2 (.a(in_1), .b({32{1'b0}}), .eq(comparator_2_eq));  // open: gt, lt
  Multiplexer #(.width(31), .enable("false")) multiplexer_4 (
    .in0({31{1'b1}}), .in1({31{1'b0}}), .out(multiplexer_4_out), .sel(in_1[31]));
  Multiplexer #(.width(32), .enable("false")) multiplexer_5 (
    .in0(multiplexer_3_out), .in1({32{1'b0}}), .out(multiplexer_5_out), .sel(comparator_2_eq));
  Multiplexer #(.width(32), .enable("false")) multiplexer_6 (
    .in0(multiplexer_5_out), .in1(multiplexer_7_out), .out(out_3), .sel(comparator_1_eq));
  Multiplexer #(.width(32), .enable("false")) multiplexer_7 (
    .in0({last, multiplexer_4_out}), .in1({last, {31{1'b0}}}), .out(multiplexer_7_out), .sel(comparator_3_eq));
  Comparator #(.width(32)) comparator_3 (.a(in_1), .b({32{1'b0}}), .eq(comparator_3_eq));  // open: gt, lt
  // Probe on out_3

  // Other names for the same wires on the sheet: NUM_1[30:0] = in_1[30:0]; NUM_1_z[31:0] = in_1;
  //   NUM_1_last = in_1[31]; NUM_2[30:0] = in_2[30:0]; NUM_2_z[31:0] = in_2; NUM_2_last = in_2[31]
endmodule

module u_CONTROL_R (
  input  [27:0] in_1,
  output out_2,
  output [4:0] RD,
  output [4:0] RS,
  output [4:0] RI,
  output [16:0] out_6
);


  assign out_2 = in_1[27];
  assign out_6 = in_1[16:0];
  assign RD = in_1[26:22];
  assign RI = in_1[4:0];
  assign RS = in_1[21:17];

  // Other names for the same wires on the sheet: IMM[16:0] = in_1[16:0]; _27_R = in_1[27]
endmodule

module u_CONTROL_J (
  input  [27:0] in_1,
  output out_2,
  output [2:0] JC,
  output [4:0] RI,
  output [23:0] out_5
);


  assign JC = in_1[26:24];
  assign out_2 = in_1[27];
  assign out_5 = in_1[23:0];
  assign RI = in_1[4:0];

  // Other names for the same wires on the sheet: IMM_j[23:0] = in_1[23:0]; _27_J = in_1[27]
endmodule

module u_JUMPS (
  input  [31:0] in_1,
  input  [2:0] in_2,
  output out_3
);

  wire JEQ, JGE, JGT, JLE, JLT, JNE, u_jeq_2_out_2, u_jgt_2_out_2, u_jlt_2_out_2;

  u_JGT u_jgt_1 (.in_1(in_1), .out_2(JGT));
  u_JEQ u_jeq_1 (.in_1(in_1), .out_2(JEQ));
  u_JLT u_jlt_1 (.in_1(in_1), .out_2(JLT));
  u_JGT u_jgt_2 (.in_1(in_1), .out_2(u_jgt_2_out_2));
  not not_1 (JLE, u_jgt_2_out_2);
  u_JEQ u_jeq_2 (.in_1(in_1), .out_2(u_jeq_2_out_2));
  not not_2 (JNE, u_jeq_2_out_2);
  u_JLT u_jlt_2 (.in_1(in_1), .out_2(u_jlt_2_out_2));
  not not_3 (JGE, u_jlt_2_out_2);
  Multiplexer #(.select(3)) multiplexer_1 (
    .in0(1'b1), .in1(JGT), .in2(JEQ), .in3(JLT), .in4(JLE), .in5(JNE), .in6(JGE), .in7(1'b1), .out(out_3),
    .sel(in_2));  // open: en

  // Other names for the same wires on the sheet: JC[31:0] = in_1
endmodule

module u_JGT (
  input  [31:0] in_1,
  output out_2
);

  Comparator #(.width(32)) comparator_1 (.a(in_1), .b({32{1'b0}}), .gt(out_2));  // open: eq, lt
endmodule

module u_JEQ (
  input  [31:0] in_1,
  output out_2
);

  Comparator #(.width(32)) comparator_1 (.a(in_1), .b({32{1'b0}}), .eq(out_2));  // open: gt, lt
endmodule

module u_JLT (
  input  [31:0] in_1,
  output out_2
);

  Comparator #(.width(32)) comparator_1 (.a(in_1), .b({32{1'b0}}), .lt(out_2));  // open: gt, eq
endmodule

module u_REV_main (
  input  [31:0] in_1,
  input  [4:0] in_2,
  output [31:0] out_3
);

  wire [31:0] u_rev_1_1_output, u_rev_2_1_output, u_rev_4_1_output, u_rev_8_1_output;

  u_REV_1 u_rev_1_1 (.in_1(in_2[0]), .INPUT(in_1), .OUTPUT(u_rev_1_1_output));
  u_REV_2 u_rev_2_1 (.INPUT(u_rev_1_1_output), .in_1(in_2[1]), .OUTPUT(u_rev_2_1_output));
  u_REV_4 u_rev_4_1 (.INPUT(u_rev_2_1_output), .in_1(in_2[2]), .OUTPUT(u_rev_4_1_output));
  u_REV_8 u_rev_8_1 (.INPUT(u_rev_4_1_output), .in_1(in_2[3]), .OUTPUT(u_rev_8_1_output));
  u_REV_16 u_rev_16_1 (.INPUT(u_rev_8_1_output), .in_1(in_2[4]), .OUTPUT(out_3));
endmodule

module u_REV_1 (
  input  in_1,
  input  [31:0] INPUT,
  output [31:0] OUTPUT
);

  Multiplexer #(.width(32), .enable("false")) multiplexer_1 (
    .in0(INPUT),
    .in1({INPUT[30], INPUT[31], INPUT[28], INPUT[29], INPUT[26], INPUT[27], INPUT[24], INPUT[25], INPUT[22], INPUT[23], INPUT[20], INPUT[21], INPUT[18], INPUT[19], INPUT[16], INPUT[17], INPUT[14], INPUT[15], INPUT[12], INPUT[13], INPUT[10], INPUT[11], INPUT[8], INPUT[9], INPUT[6], INPUT[7], INPUT[4], INPUT[5], INPUT[2], INPUT[3], INPUT[0], INPUT[1]}),
    .out(OUTPUT), .sel(in_1));
endmodule

module u_REV_2 (
  input  in_1,
  input  [31:0] INPUT,
  output [31:0] OUTPUT
);

  Multiplexer #(.width(32), .enable("false")) multiplexer_1 (
    .in0(INPUT),
    .in1({INPUT[29:28], INPUT[31:30], INPUT[25:24], INPUT[27:26], INPUT[21:20], INPUT[23:22], INPUT[17:16], INPUT[19:18], INPUT[13:12], INPUT[15:14], INPUT[9:8], INPUT[11:10], INPUT[5:4], INPUT[7:6], INPUT[1:0], INPUT[3:2]}),
    .out(OUTPUT), .sel(in_1));
endmodule

module u_REV_4 (
  input  in_1,
  input  [31:0] INPUT,
  output [31:0] OUTPUT
);

  Multiplexer #(.width(32), .enable("false")) multiplexer_1 (
    .in0(INPUT),
    .in1({INPUT[27:24], INPUT[31:28], INPUT[19:16], INPUT[23:20], INPUT[11:8], INPUT[15:12], INPUT[3:0], INPUT[7:4]}),
    .out(OUTPUT), .sel(in_1));
endmodule

module u_REV_8 (
  input  in_1,
  input  [31:0] INPUT,
  output [31:0] OUTPUT
);

  Multiplexer #(.width(32), .enable("false")) multiplexer_1 (
    .in0(INPUT), .in1({INPUT[23:16], INPUT[31:24], INPUT[7:0], INPUT[15:8]}), .out(OUTPUT), .sel(in_1));
endmodule

module u_REV_16 (
  input  in_1,
  input  [31:0] INPUT,
  output [31:0] OUTPUT
);

  Multiplexer #(.width(32), .enable("false")) multiplexer_1 (
    .in0(INPUT), .in1({INPUT[15:0], INPUT[31:16]}), .out(OUTPUT), .sel(in_1));
endmodule

module u_SR (
  input  [31:0] in_1,
  input  [31:0] in_2,
  output [31:0] out_3
);

  Shifter #(.width(32), .shift("ar")) shifter_1 (.in(in_1), .\dist (in_2[4:0]), .out(out_3));
endmodule

module u_STU (
  input  [31:0] in_1,
  input  [31:0] in_2,
  output [31:0] out_3
);


  assign out_3 = {in_2[16:0], in_1[14:0]};
endmodule
